# Fritzing sketch atmegaprogrammer (saved by Fritzing 0.9.3b)
circuit board: 5.64cm x 5.64444cm
breadboards: 1

parts:
  ATmega328 = atmega328 [package=dip]
  S1 = Toggle Switch [package=THT]
  part = Toggle Switch [package=THT]  # not connected
  R3 = Resistor [tolerance=±5% resistance=100 package=THT]
  LED_HEART = LED - 5mm [color="Blue (430nm)" package="5 mm [THT]"]
  LED_ERR = LED - 5mm [color="Red (633nm)" package="5 mm [THT]"]
  C1 = Ceramic Capacitor [capacitance=100nF package="200 mil [THT, multilayer]"]
  R5 = Resistor [tolerance=±5% resistance=100 package=THT]
  LED_TEST = LED - 5mm [color="Yellow (585nm)" package="5 mm [THT]"]
  R1 = Resistor [tolerance=±5% resistance=10k package=THT]
  R2 = Resistor [tolerance=±5% resistance=100 package=THT]
  R4 = Resistor [tolerance=±5% resistance=100 package=THT]
  C2 = Ceramic Capacitor [capacitance=100nF package="200 mil [THT, multilayer]"]
  LED_OK = LED - 5mm [color="Green (555nm)" package="5 mm [THT]"]
  J5 = female pin header, 2 pins [form="♀ (female)"]
  J4 = female pin header, 2 pins [form="♀ (female)"]
  J3 = female pin header, 2 pins [form="♀ (female)"]
  J2 = female pin header, 2 pins [form="♀ (female)"]
  J1 = female pin header, 2 pins [form="♀ (female)"]
  XTAL1 = Crystal [frequency="16 Mhz" package=THT]

nets:
  N1: ATmega328.RESET, R1.Pin_1, J2.pin2
  N2: ATmega328.VCC, ATmega328.AVCC, R1.Pin_0, J4.pin2
  N3: ATmega328.GND, LED_HEART.cathode, LED_ERR.cathode, C1.0, LED_TEST.cathode, C2.1, LED_OK.cathode, J4.pin1
  N4: ATmega328.XLAT1, C1.1, XTAL1.pin_0
  N5: ATmega328.XLAT2, S1.COM
  N6: ATmega328.D8, R5.Pin_0
  N7: ATmega328.D11_(PWM), J2.pin1
  N8: ATmega328.D12, J1.pin2
  N9: ATmega328.D13, J1.pin1
  N10: S1.L2, C2.0, XTAL1.pin_1
  N11: R3.Pin_0, LED_OK.anode
  N12: R3.Pin_1, J3.pin1
  N13: LED_HEART.anode, R4.Pin_1
  N14: LED_ERR.anode, R2.Pin_1
  N15: R5.Pin_1, LED_TEST.anode
  N16: R2.Pin_0, J5.pin2
  N17: R4.Pin_0, J5.pin1
