# Fritzing sketch atmegaprogrammer_connected (saved by Fritzing 0.9.3b)
circuit board: 5.64cm x 5.64444cm
breadboards: 1

parts:
  ATmega328 = atmega328 [package=dip]
  S1 = Toggle Switch [package=THT]
  R3 = Resistor [tolerance=±5% resistance=100 package=THT]
  LED_HEART = LED - 5mm [color="Blue (430nm)" package="5 mm [THT]"]
  LED_ERR = LED - 5mm [color="Red (633nm)" package="5 mm [THT]"]
  C1 = Ceramic Capacitor [capacitance=100nF package="200 mil [THT, multilayer]"]
  R5 = Resistor [tolerance=±5% resistance=100 package=THT]
  LED_TEST = LED - 5mm [color="Yellow (585nm)" package="5 mm [THT]"]
  R1 = Resistor [tolerance=±5% resistance=10k package=THT]
  R2 = Resistor [tolerance=±5% resistance=100 package=THT]
  R4 = Resistor [tolerance=±5% resistance=100 package=THT]
  C2 = Ceramic Capacitor [capacitance=100nF package="200 mil [THT, multilayer]"]
  LED_OK = LED - 5mm [color="Green (555nm)" package="5 mm [THT]"]
  XTAL1 = Crystal [frequency="16 Mhz" package=THT]
  Bauteil1 = Arduino Uno (Rev3)

nets:
  N1: ATmega328.RESET, R1.Pin_1, Bauteil1.D10_PWM/SS
  VCC: ATmega328.VCC, ATmega328.AVCC, R1.Pin_0, Bauteil1.5V
  GND: ATmega328.GND, LED_HEART.cathode, LED_ERR.cathode, C1.0, LED_TEST.cathode, C2.1, LED_OK.cathode, Bauteil1.GND
  N2: ATmega328.XLAT1, C1.1, XTAL1.pin_0
  N3: ATmega328.XLAT2, S1.COM
  N4: ATmega328.D8, R5.Pin_0
  N5: ATmega328.D11_(PWM), Bauteil1.D11_PWM/MOSI
  N6: ATmega328.D12, Bauteil1.D12/MISO
  N7: ATmega328.D13, Bauteil1.D13/SCK
  N8: S1.L2, C2.0, XTAL1.pin_1
  N9: R3.Pin_0, LED_OK.anode
  N10: R3.Pin_1, Bauteil1.D6_PWM
  N11: LED_HEART.anode, R4.Pin_1
  N12: LED_ERR.anode, R2.Pin_1
  N13: R5.Pin_1, LED_TEST.anode
  N14: R2.Pin_0, Bauteil1.D7
  N15: R4.Pin_0, Bauteil1.D9_PWM
